// Logisim project GOAT 4BitALU.circ as structural Verilog: 10 circuits, main circuit 4-Bit ALU
module _4_Bit_ALU (
  input  A3,
  input  A2,
  input  A1,
  input  A0,
  input  B3,
  input  B2,
  input  B1,
  input  B0,
  input  S2,
  input  S1,
  input  S0,
  output OF,
  output R3,
  output R2,
  output R1,
  output R0
);

  wire [3:0] interface_1_r, undriven, undriven_2;

  Hex_Digit_Display hex_digit_display_1 (.value(undriven), .dp(1'b0));
  Hex_Digit_Display hex_digit_display_2 (.value(undriven_2), .dp(1'b0));
  Interface interface_1 (
    .A3(A3), .R3(R3), .A2(A2), .R2(R2), .A1(A1), .R1(R1), .A0(A0), .R0(R0), .B3(B3), .B2(B2), .B1(B1),
    .B0(B0), .S2(S2), .S1(S1), .S0(S0), .R(interface_1_r), .OF(OF));  // open: A, B
  Hex_Digit_Display hex_digit_display_3 (.value(interface_1_r), .dp(1'b0));

  // Notes on the sheet:
  //   Kleinprojekt Arithmetic and Logic Unit
  //   Teamname:
  //   ausgeführt von
  //   kelvin.louis@students.fhnw.ch
  //   nicola.cocquio@students.fhnw.ch
  //   raphael.roussis@students.fhnw.ch
  //   vladimir.nikitovic@students.fhnw.ch
  //   GOAT
endmodule

module Interface (
  input  A0,
  input  A1,
  input  A2,
  input  A3,
  input  B0,
  input  B1,
  input  B2,
  input  B3,
  input  S0,
  input  S1,
  input  S2,
  output [3:0] A,
  output [3:0] R,
  output R0,
  output R1,
  output R2,
  output R3,
  output [3:0] B,
  output OF
);

  wire decoder_1_out0, decoder_1_out1, decoder_1_out2, decoder_1_out3, decoder_1_out4, decoder_1_out5,
       decoder_1_out6, decoder_1_out7;
  wire [2:0] n3_bit_splitter_1_out_4;

  _4_Bit_Splitter u_4_bit_splitter_1 (.X0(A0), .X1(A1), .X2(A2), .X3(A3), .out_5(A));
  _4_Bit_Splitter u_4_bit_splitter_2 (.X0(B0), .X1(B1), .X2(B2), .X3(B3), .out_5(B));
  _3_Bit_Splitter u_3_bit_splitter_1 (.X0(S0), .X1(S1), .X2(S2), .out_4(n3_bit_splitter_1_out_4));
  Decoder #(.select(3), .disabled(0), .enable("false")) decoder_1 (
    .out0(decoder_1_out0), .out1(decoder_1_out1), .out2(decoder_1_out2), .out3(decoder_1_out3),
    .out4(decoder_1_out4), .out5(decoder_1_out5), .out6(decoder_1_out6), .out7(decoder_1_out7),
    .sel(n3_bit_splitter_1_out_4));
endmodule

module blackbox (
);

  _4_Bit_ALU u_4_bit_alu_1 ();  // open: A3, A2, A1, A0, B3, B2, B1, B0, S2, S1, S0, OF, R3, R2, R1, R0
endmodule

module _4_Bit_OR (
  input  A0,
  input  B0,
  input  A1,
  input  B1,
  input  A2,
  input  B2,
  input  A3,
  input  B3,
  output R0,
  output R1,
  output R2,
  output R3
);

  or or_1 (R0, A0, B0);
  or or_2 (R1, A1, B1);
  or or_3 (R2, A2, B2);
  or or_4 (R3, A3, B3);

  // Notes on the sheet:
  //   4-Bit OR
endmodule

module _4_Bit_AND (
  input  A0,
  input  B0,
  input  A1,
  input  B1,
  input  A2,
  input  B2,
  input  A3,
  input  B3,
  output R0,
  output R1,
  output R2,
  output R3
);

  and and_1 (R0, A0, B0);
  and and_2 (R1, A1, B1);
  and and_3 (R2, A2, B2);
  and and_4 (R3, A3, B3);

  // Notes on the sheet:
  //   4-Bit AND
endmodule

module _4_Bit_NOT (
  input  X0,
  input  X1,
  input  X2,
  input  X3,
  output R0,
  output R1,
  output R2,
  output R3
);

  not not_1 (R0, X0);
  not not_2 (R1, X1);
  not not_3 (R2, X2);
  not not_4 (R3, X3);

  // Notes on the sheet:
  //   4-Bit NOT
endmodule

module VA (
  input  x1,
  input  x0,
  input  ci,
  output co,
  output s
);

  wire ha_1_c, ha_1_s, ha_2_c;

  HA ha_1 (.x1(x1), .x0(x0), .c(ha_1_c), .s(ha_1_s));
  HA ha_2 (.x1(ha_1_s), .x0(ci), .c(ha_2_c), .s(s));
  or or_1 (co, ha_1_c, ha_2_c);

  // Notes on the sheet:
  //   VA: Volladdierer
endmodule

module HA (
  input  x1,
  input  x0,
  output c,
  output s
);

  and and_1 (c, x1, x0);
  xor xor_1 (s, x1, x0);

  // Notes on the sheet:
  //   HA: Halbaddierer
endmodule

module _3_Bit_Splitter (
  input  X0,
  input  X1,
  input  X2,
  output [2:0] out_4
);


  assign out_4 = {X2, X1, X0};

  // Notes on the sheet:
  //   3-Bit Splitter
endmodule

module _4_Bit_Splitter (
  input  X0,
  input  X1,
  input  X2,
  input  X3,
  output [3:0] out_5
);


  assign out_5 = {X3, X2, X1, X0};

  // Notes on the sheet:
  //   4-Bit Splitter
endmodule
